# Fritzing sketch DIAGRAMA EN FRITZING (saved by Fritzing 0.9.3b)

parts:
  Componente1 = Arduino Uno (Rev3) - ICSP
  RELAY1 = CAR RELAY [part_number=NVF4-2 package=THT]
  RELAY2 = CAR RELAY [part_number=NVF4-2 package=THT]
  WeMos_D1_Mini_Relay_Shield_V1 = WeMos D1 Mini Relay Shield V2
  WeMos_D1_Mini_Relay_Shield_V2 = WeMos D1 Mini Relay Shield V2
  U1 = SWITCH_SPDT [package=kps-1290]
  U2 = SWITCH_SPDT [package=kps-1290]
  U3 = LCD-16X2 [package=lcd-16x2]
  U4 = LIPO-2000mAh [package=lipo-2000]
  J1 = Basic Servo
  BAT1 = BC9VPC [package=bc9vpc]
  U5 = LIS302DL [package=lga14]
  M1 = DC Motor

nets:
  N1: Componente1.A4/SDA, U5.SCL_SPC
  N2: Componente1.A5/SCL, U5.SDA_SDI
  GND: Componente1.GND, WeMos_D1_Mini_Relay_Shield_V1.G, WeMos_D1_Mini_Relay_Shield_V2.G, U1.S, U2.S, U3.VSS, J1.gnd, BAT1.V-, U5.VDD_IO
  N3: Componente1.D8, J1.pulse
  N4: Componente1.D4, WeMos_D1_Mini_Relay_Shield_V2.RX
  N5: Componente1.D5_PWM, WeMos_D1_Mini_Relay_Shield_V1.RX
  N6: Componente1.D6_PWM, U2.P
  N7: Componente1.D7, U1.P
  5V: Componente1.5V, J1.vcc
  N8: RELAY1.87A, RELAY1.86, RELAY2.87A, RELAY2.86, U4.-
  N9: RELAY1.85, WeMos_D1_Mini_Relay_Shield_V1.COM
  N10: RELAY1.30, M1.pin_1
  N11: RELAY1.87, RELAY2.87, WeMos_D1_Mini_Relay_Shield_V1.NO, WeMos_D1_Mini_Relay_Shield_V2.NO, U4.+
  N12: RELAY2.85, WeMos_D1_Mini_Relay_Shield_V2.COM
  N13: RELAY2.30, M1.pin_2
  N14: U3.VO, U3.R_W, U3.E, U3.DB4, U3.DB5, U5.GND
  N15: U3.RS, U3.DB0, U5.VDD
  N16: U3.DB1, U5.CS
  N17: U3.DB2, U5.INT1
  N18: U3.DB3, U5.INT2
  N19: U3.DB6, U5.SDO
